# Fritzing sketch schematic (saved by Fritzing 0.9.3b)
breadboards: 2

parts:
  Part1 = Arduino Uno (Rev3) - ICSP
  R1 = Temperature Sensor (Thermistor) [thermistor_type=NTC package=THT]
  R2 = Resistor [tolerance=±5% resistance=10k package="2010 [SMD]"]
  U1 = LCD-16X2 [package=lcd-16x2_noholes]
  R3 = Resistor [tolerance=±5% resistance=2.2k package="2010 [SMD]"]
  R4 = Resistor [tolerance=±5% resistance=220 package="2010 [SMD]"]
  RGB-LED1 = RGB LED (com. cathode, rgb) [package="5 mm [THT]"]
  J1 = Piezo Speaker [part_number=Speaker]
  Part2 = Adafruit ADS1115 16Bit I2C ADC [part_number="Adafruit #1085"]

nets:
  N1: Part1.A0, R1.pin_0, R2.Pin_1, Part2.AIN0
  N2: Part1.A4/SDA, Part2.SDA
  N3: Part1.A5/SCL, Part2.SCL
  VDD: Part1.5V, R1.pin_1, U1.VDD, R4.Pin_0, Part2.VDD
  N4: Part1.D8, RGB-LED1.red_anode
  N5: Part1.D9_PWM, RGB-LED1.green_anode
  N6: Part1.D10_PWM/SS, RGB-LED1.blue_anode
  N7: Part1.D11_PWM/MOSI, U1.E
  N8: Part1.D12/MISO, U1.RS
  GND: Part1.GND, R2.Pin_0, U1.VSS, U1.R_W, U1.K, R3.Pin_0, RGB-LED1.common_cathode, J1.pin2, Part2.GND
  N9: Part1.D2, U1.DB7
  N10: Part1.D3_PWM, U1.DB6
  N11: Part1.D4, U1.DB5
  N12: Part1.D5_PWM, U1.DB4
  N13: Part1.D7, J1.pin1
  N14: U1.VO, R3.Pin_1
  N15: U1.A, R4.Pin_1

custom parts:
  Adafruit ADS1115 16Bit I2C ADC: For microcontrollers without an analog-to-digital converter or when you want a higher-precision ADC, the ADS1115 provides 16-bit precision at 860 samples/second over I2C. The chip can be configured as 4 single-ended input channels, or two differential channels. As a nice bonus, it even includes a programmable gain amplifier, up to x16, to help boost up smaller single/differential signals to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
